# Fritzing sketch eventsAndSleep (saved by Fritzing 0.9.2b)
breadboards: 1

parts:
  Part1 = Arduino Uno (Rev3)
  S1 = Pushbutton [package="[THT]"]
  R1 = Resistor [tolerance=±5% resistance=330 package=THT]

nets:
  N1: Part1.D3_PWM, S1.Pin_3, S1.Pin_4, R1.Pin_1
  N2: Part1.5V, R1.Pin_0
  N3: Part1.GND, S1.Pin_1, S1.Pin_2
